// Logisim project HW1-403106238.circ as structural Verilog: 14 circuits, main circuit main
module main (
  input  [31:0] A,
  input  [31:0] B,
  input  [2:0] ALU_Ctrl,
  output [31:0] Result_Lo,
  output [31:0] Result_Hi,
  output Z,
  output C,
  output N,
  output V
);

  ALU_32bit ALU (
    .A(A), .B(B), .ALU_Ctrl(ALU_Ctrl), .Result_Lo(Result_Lo), .Result_Hi(Result_Hi), .Z(Z), .C(C), .N(N),
    .V(V));
endmodule

module FA (
  input  A,
  input  B,
  input  c_in,
  output S,
  output c_out
);

  wire and_1_out, and_2_out, and_3_out;

  and and_1 (and_1_out, A, c_in);
  and and_2 (and_2_out, B, c_in);
  and and_3 (and_3_out, B, A);
  xor xor_1 (S, A, B, c_in);
  or or_1 (c_out, and_1_out, and_2_out, and_3_out);
endmodule

module adder_8bit (
  input  [7:0] A,
  input  [7:0] B,
  input  c_in,
  input  sub,
  output [7:0] S,
  output c_out
);

  wire FA0_c_out, FA1_c_out, FA2_c_out, FA3_c_out, FA4_c_out, FA5_c_out, FA6_c_out, xor_1_out, xor_2_out,
       xor_3_out, xor_4_out, xor_5_out, xor_6_out, xor_7_out, xor_8_out;

  xor xor_1 (xor_1_out, B[0], sub);
  xor xor_2 (xor_2_out, B[1], sub);
  xor xor_3 (xor_3_out, B[2], sub);
  xor xor_4 (xor_4_out, B[3], sub);
  xor xor_5 (xor_5_out, B[4], sub);
  xor xor_6 (xor_6_out, B[5], sub);
  xor xor_7 (xor_7_out, B[6], sub);
  xor xor_8 (xor_8_out, B[7], sub);
  FA FA0 (.A(A[0]), .B(xor_1_out), .c_in(c_in), .S(S[0]), .c_out(FA0_c_out));
  FA FA1 (.A(A[1]), .B(xor_2_out), .c_in(FA0_c_out), .S(S[1]), .c_out(FA1_c_out));
  FA FA2 (.A(A[2]), .B(xor_3_out), .c_in(FA1_c_out), .S(S[2]), .c_out(FA2_c_out));
  FA FA3 (.A(A[3]), .B(xor_4_out), .c_in(FA2_c_out), .S(S[3]), .c_out(FA3_c_out));
  FA FA4 (.A(A[4]), .B(xor_5_out), .c_in(FA3_c_out), .S(S[4]), .c_out(FA4_c_out));
  FA FA5 (.A(A[5]), .B(xor_6_out), .c_in(FA4_c_out), .S(S[5]), .c_out(FA5_c_out));
  FA FA6 (.A(A[6]), .B(xor_7_out), .c_in(FA5_c_out), .S(S[6]), .c_out(FA6_c_out));
  FA FA7 (.A(A[7]), .B(xor_8_out), .c_in(FA6_c_out), .S(S[7]), .c_out(c_out));
endmodule

module adder_32bit (
  input  [31:0] A,
  input  [31:0] B,
  input  sub,
  output [31:0] S,
  output c_out
);

  wire adder_0_c_out, adder_1_c_out, adder_2_c_out;

  adder_8bit adder_0 (.A(A[7:0]), .B(B[7:0]), .c_in(sub), .sub(sub), .S(S[7:0]), .c_out(adder_0_c_out));
  adder_8bit adder_1 (.A(A[15:8]), .B(B[15:8]), .c_in(adder_0_c_out), .sub(sub), .S(S[15:8]), .c_out(adder_1_c_out));
  adder_8bit adder_2 (.A(A[23:16]), .B(B[23:16]), .c_in(adder_1_c_out), .sub(sub), .S(S[23:16]), .c_out(adder_2_c_out));
  adder_8bit adder_3 (.A(A[31:24]), .B(B[31:24]), .c_in(adder_2_c_out), .sub(sub), .S(S[31:24]), .c_out(c_out));
endmodule

module mul_4bit (
  input  [3:0] A,
  input  [3:0] B,
  output [7:0] mul
);

  wire FA1_c_out, FA2_c_out, FA2_s, FA3_c_out, FA3_s, FA4_c_out, FA4_s, FA5_c_out, FA6_c_out, FA7_c_out,
       HA1_c, HA2_c, HA2_s, HA3_c, HA3_s, HA4_c, HA4_s, m01, m02, m03, m10, m11, m12, m13, m20, m21, m22,
       m23, m30, m31, m32, m33;

  and and_1 (mul[0], B[0], A[0]);
  and and_2 (m10, B[0], A[1]);
  and and_3 (m20, B[0], A[2]);
  and and_4 (m30, B[0], A[3]);
  HA HA1 (.A(m01), .B(m10), .S(mul[1]), .C(HA1_c));
  HA HA2 (.A(m02), .B(HA1_c), .S(HA2_s), .C(HA2_c));
  HA HA3 (.A(m03), .B(HA2_c), .S(HA3_s), .C(HA3_c));
  HA HA4 (.A(m13), .B(HA3_c), .S(HA4_s), .C(HA4_c));
  and and_5 (m01, B[1], A[0]);
  and and_6 (m11, B[1], A[1]);
  and and_7 (m21, B[1], A[2]);
  and and_8 (m31, B[1], A[3]);
  and and_9 (m02, B[2], A[0]);
  and and_10 (m12, B[2], A[1]);
  and and_11 (m22, B[2], A[2]);
  and and_12 (m32, B[2], A[3]);
  FA FA1 (.A(m20), .B(m11), .c_in(HA2_s), .S(mul[2]), .c_out(FA1_c_out));
  FA FA2 (.A(m12), .B(FA1_c_out), .c_in(HA3_s), .S(FA2_s), .c_out(FA2_c_out));
  FA FA3 (.A(m22), .B(FA2_c_out), .c_in(HA4_s), .S(FA3_s), .c_out(FA3_c_out));
  FA FA4 (.A(m23), .B(FA3_c_out), .c_in(HA4_c), .S(FA4_s), .c_out(FA4_c_out));
  and and_13 (m03, B[3], A[0]);
  and and_14 (m13, B[3], A[1]);
  and and_15 (m23, B[3], A[2]);
  and and_16 (m33, B[3], A[3]);
  FA FA5 (.A(m30), .B(m21), .c_in(FA2_s), .S(mul[3]), .c_out(FA5_c_out));
  FA FA6 (.A(m31), .B(FA5_c_out), .c_in(FA3_s), .S(mul[4]), .c_out(FA6_c_out));
  FA FA7 (.A(m32), .B(FA6_c_out), .c_in(FA4_s), .S(mul[5]), .c_out(FA7_c_out));
  FA FA8 (.A(m33), .B(FA7_c_out), .c_in(FA4_c_out), .S(mul[6]), .c_out(mul[7]));

  // Other names for the same wires on the sheet: c0 = mul[0]; m00 = mul[0]; c1 = mul[1]; c2 = mul[2]; c3 = mul[3];
  //   c4 = mul[4]; c5 = mul[5]; c6 = mul[6]; c7 = mul[7]
endmodule

module HA (
  input  A,
  input  B,
  output S,
  output C
);

  and and_1 (C, A, B);
  xor xor_1 (S, B, A);
endmodule

module mul_8bit (
  input  [7:0] A,
  input  [7:0] B,
  output [15:0] M
);

  wire add_2_c_out;
  wire [4:4] add_1_c_out;
  wire [7:0] add_1_s, P_HH_mul, P_HL_mul, P_LH_mul;
  wire [7:4] P_LL_mul;

  mul_4bit P_LL (.A(A[3:0]), .B(B[3:0]), .mul({P_LL_mul, M[3:0]}));
  mul_4bit P_LH (.A(A[3:0]), .B(B[7:4]), .mul(P_LH_mul));
  mul_4bit P_HL (.A(A[7:4]), .B(B[3:0]), .mul(P_HL_mul));
  mul_4bit P_HH (.A(A[7:4]), .B(B[7:4]), .mul(P_HH_mul));
  adder_8bit add_1 (.A(P_LH_mul), .B(P_HL_mul), .c_in(1'b0), .sub(1'b0), .S(add_1_s), .c_out(add_1_c_out[4]));
  adder_4bit add_2 (.A(P_LL_mul), .B(add_1_s[3:0]), .c_in(1'b0), .S(M[7:4]), .c_out(add_2_c_out));
  adder_8bit add_3 (
    .A({3'b000, add_1_c_out[4], add_1_s[7:4]}), .B(P_HH_mul), .c_in(add_2_c_out), .sub(1'b0), .S(M[15:8]));  // open: c_out
endmodule

module adder_4bit (
  input  [3:0] A,
  input  [3:0] B,
  input  c_in,
  output [3:0] S,
  output c_out
);

  wire FA1_c_out, FA2_c_out, FA3_c_out;

  FA FA1 (.A(A[0]), .B(B[0]), .c_in(c_in), .S(S[0]), .c_out(FA1_c_out));
  FA FA2 (.A(A[1]), .B(B[1]), .c_in(FA1_c_out), .S(S[1]), .c_out(FA2_c_out));
  FA FA3 (.A(A[2]), .B(B[2]), .c_in(FA2_c_out), .S(S[2]), .c_out(FA3_c_out));
  FA FA4 (.A(A[3]), .B(B[3]), .c_in(FA3_c_out), .S(S[3]), .c_out(c_out));
endmodule

module mul_16bit (
  input  [15:0] A,
  input  [15:0] B,
  output [31:0] M
);

  wire add_2_c_out;
  wire [8:8] add_1_c_out;
  wire [15:0] add_1_s, mul_2_m, mul_3_m, mul_4_m;
  wire [15:8] mul_1_m;

  mul_8bit mul_1 (.A(A[7:0]), .B(B[7:0]), .M({mul_1_m, M[7:0]}));
  mul_8bit mul_2 (.A(A[15:8]), .B(B[7:0]), .M(mul_2_m));
  mul_8bit mul_3 (.A(A[7:0]), .B(B[15:8]), .M(mul_3_m));
  mul_8bit mul_4 (.A(A[15:8]), .B(B[15:8]), .M(mul_4_m));
  adder_16bit add_1 (.A(mul_2_m), .B(mul_3_m), .c_in(1'b0), .S(add_1_s), .c_out(add_1_c_out[8]));
  adder_8bit add_2 (.A(mul_1_m), .B(add_1_s[7:0]), .c_in(1'b0), .sub(1'b0), .S(M[15:8]), .c_out(add_2_c_out));
  adder_16bit add_3 (
    .A({{7{1'b0}}, add_1_c_out[8], add_1_s[15:8]}), .B(mul_4_m), .c_in(add_2_c_out), .S(M[31:16]));  // open: c_out
endmodule

module adder_16bit (
  input  [15:0] A,
  input  [15:0] B,
  input  c_in,
  output [15:0] S,
  output c_out
);

  wire add_1_c_out;

  adder_8bit add_1 (.A(A[7:0]), .B(B[7:0]), .c_in(c_in), .sub(1'b0), .S(S[7:0]), .c_out(add_1_c_out));
  adder_8bit add_2 (.A(A[15:8]), .B(B[15:8]), .c_in(add_1_c_out), .sub(1'b0), .S(S[15:8]), .c_out(c_out));
endmodule

module mul_32bit (
  input  [31:0] A,
  input  [31:0] B,
  output [31:0] Lo,
  output [31:0] Hi
);

  wire add_2_c_out;
  wire [16:16] add_1_c_out;
  wire [31:0] add_1_s, mul_2_m, mul_3_m, mul_4_m;
  wire [31:16] mul_1_m;

  mul_16bit mul_1 (.A(A[15:0]), .B(B[15:0]), .M({mul_1_m, Lo[15:0]}));
  mul_16bit mul_2 (.A(A[31:16]), .B(B[15:0]), .M(mul_2_m));
  mul_16bit mul_3 (.A(A[15:0]), .B(B[31:16]), .M(mul_3_m));
  mul_16bit mul_4 (.A(A[31:16]), .B(B[31:16]), .M(mul_4_m));
  adder_32bit add_1 (.A(mul_2_m), .B(mul_3_m), .sub(1'b0), .S(add_1_s), .c_out(add_1_c_out[16]));
  adder_16bit add_2 (.A(mul_1_m), .B(add_1_s[15:0]), .c_in(1'b0), .S(Lo[31:16]), .c_out(add_2_c_out));
  adder_32bit_no_sub add_3 (
    .A({{15{1'b0}}, add_1_c_out[16], add_1_s[31:16]}), .B(mul_4_m), .c_in(add_2_c_out), .S(Hi));  // open: c_out
endmodule

module adder_32bit_no_sub (
  input  [31:0] A,
  input  [31:0] B,
  input  c_in,
  output [31:0] S,
  output c_out
);

  wire add_1_c_out, add_2_c_out, add_3_c_out;

  adder_8bit add_1 (.A(A[7:0]), .B(B[7:0]), .c_in(c_in), .sub(1'b0), .S(S[7:0]), .c_out(add_1_c_out));
  adder_8bit add_2 (.A(A[15:8]), .B(B[15:8]), .c_in(add_1_c_out), .sub(1'b0), .S(S[15:8]), .c_out(add_2_c_out));
  adder_8bit add_3 (.A(A[23:16]), .B(B[23:16]), .c_in(add_2_c_out), .sub(1'b0), .S(S[23:16]), .c_out(add_3_c_out));
  adder_8bit add_4 (.A(A[31:24]), .B(B[31:24]), .c_in(add_3_c_out), .sub(1'b0), .S(S[31:24]), .c_out(c_out));
endmodule

module ALU_32bit (
  input  [31:0] A,
  input  [31:0] B,
  input  [2:0] ALU_Ctrl,
  output [31:0] Result_Lo,
  output [31:0] Result_Hi,
  output Z,
  output C,
  output N,
  output V
);

  wire add_1_c_out, and_1_out, and_2_out, and_3_out, and_4_out, and_5_out, and_6_out, and_7_out,
       multiplexer_3_out, nand_1_out, nor_1_out, nor_2_out, nor_3_out, nor_4_out, not_1_out, not_2_out,
       not_3_out, not_4_out, not_5_out, not_6_out, not_7_out, or_1_out, or_1_z, or_2_z, xor_1_out, xor_2_out,
       xor_3_out, xor_4_out;
  wire [31:0] add_1_s, add_2_hi, add_2_lo;

  xor xor_1 (xor_1_out, A[31], B[31]);
  not not_1 (not_1_out, ALU_Ctrl[2]);
  nor nor_1 (nor_1_out, ALU_Ctrl[0], ALU_Ctrl[1]);
  and and_1 (and_1_out, nor_1_out, ALU_Ctrl[2]);
  not not_2 (not_2_out, ALU_Ctrl[2]);
  not not_3 (not_3_out, xor_1_out);
  and and_2 (and_2_out, ALU_Ctrl[1], not_1_out);
  or or_1 (or_1_out, and_1_out, not_2_out);
  xor xor_2 (xor_2_out, A[31], add_1_s[31]);
  not not_4 (not_4_out, ALU_Ctrl[1]);
  not not_5 (not_5_out, ALU_Ctrl[0]);
  and and_3 (and_3_out, not_3_out, xor_2_out);
  adder_32bit add_1 (.A(A), .B(B), .sub(and_2_out), .S(add_1_s), .c_out(add_1_c_out));
  mul_32bit add_2 (.A(A), .B(B), .Lo(add_2_lo), .Hi(add_2_hi));
  and and_4 (and_4_out, ALU_Ctrl[2], not_4_out, not_5_out);
  and and_5 (and_5_out, xor_1_out, xor_2_out);
  Multiplexer #(.enable("true"), .width(32)) multiplexer_1 (
    .in0(add_1_s), .in1(add_2_lo), .out(Result_Lo), .sel(ALU_Ctrl[2]), .en(or_1_out));
  Multiplexer #(.width(32)) multiplexer_2 (.in0({32{1'b0}}), .in1(add_2_hi), .out(Result_Hi), .sel(and_4_out));
  not not_6 (not_6_out, ALU_Ctrl[2]);
  OR_32bit or_1_dup2 (.A(Result_Lo), .Z(or_1_z));
  OR_32bit or_2 (.A(Result_Hi), .Z(or_2_z));
  nor nor_2 (nor_2_out, ALU_Ctrl[0], ALU_Ctrl[2]);
  and and_6 (and_6_out, ALU_Ctrl[0], not_6_out);
  not not_7 (not_7_out, add_1_c_out);
  Multiplexer #(.select(2)) multiplexer_3 (
    .in0(add_1_c_out), .in1(and_3_out), .in2(not_7_out), .in3(and_5_out), .out(multiplexer_3_out),
    .sel(ALU_Ctrl[1:0]));
  nor nor_3 (nor_3_out, or_1_z, or_2_z);
  xor xor_3 (xor_3_out, ALU_Ctrl[1], add_1_c_out);
  xor xor_4 (xor_4_out, add_1_s[31], V);
  assign V = not_6_out ? multiplexer_3_out : 1'bz;  // Controlled_Buffer controlled_buffer_1
  assign C = nor_2_out ? xor_3_out : 1'bz;  // Controlled_Buffer controlled_buffer_2
  assign N = and_6_out ? xor_4_out : 1'bz;  // Controlled_Buffer controlled_buffer_3
  nor nor_4 (nor_4_out, ALU_Ctrl[0], ALU_Ctrl[1], ALU_Ctrl[2]);
  nand nand_1 (nand_1_out, add_1_c_out, nor_4_out);
  and and_7 (and_7_out, nor_3_out, nand_1_out);
  assign Z = or_1_out ? and_7_out : 1'bz;  // Controlled_Buffer controlled_buffer_4
endmodule

module OR_32bit (
  input  [31:0] A,
  output Z
);

  or or_1 (Z, A[0], A[1], A[2], A[3], A[4], A[5], A[6], A[7], A[8], A[9], A[10], A[11], A[12], A[13], A[14], A[15], A[16], A[17], A[18], A[19], A[20], A[21], A[22], A[23], A[24], A[25], A[26], A[27], A[28], A[29], A[30], A[31]);
endmodule
