// Logisim project HW2C-403106238.circ as structural Verilog: 5 circuits, main circuit main
module main (
  input  [31:0] Data,
  input  [1:0] Count_Op,
  output [5:0] Count
);

  wire [31:0] corrector_fixed;

  correction corrector (.A(Data), .opcode(Count_Op), .fixed(corrector_fixed));
  CTZ_32bit ctz (.A(corrector_fixed), .count(Count));  // open: all_z
endmodule

module CTZ_8bit (
  input  [7:0] A,
  output [3:0] count,
  output all_z
);

  wire multiplexer_1_out, multiplexer_2_out, multiplexer_3_out, multiplexer_4_out, or_1_out, or_2_out,
       or_3_out, or_4_out, or_5_out, or_6_out, or_7_out, or_8_out;
  wire [2:0] not_3_out;

  or or_1 (or_1_out, A[7], A[6]);
  or or_2 (or_2_out, A[5], A[4]);
  or or_3 (or_3_out, A[3], A[2]);
  or or_4 (or_4_out, A[1], A[0]);
  or or_5 (or_5_out, or_1_out, or_2_out);
  or or_6 (or_6_out, or_3_out, or_4_out);
  Multiplexer multiplexer_1 (.in0(A[6]), .in1(A[2]), .out(multiplexer_1_out), .sel(or_6_out));
  Multiplexer multiplexer_2 (.in0(A[5]), .in1(A[1]), .out(multiplexer_2_out), .sel(or_6_out));
  Multiplexer multiplexer_3 (.in0(A[4]), .in1(A[0]), .out(multiplexer_3_out), .sel(or_6_out));
  or or_7 (or_7_out, or_5_out, or_6_out);
  not not_1 (not_3_out[2], or_6_out);
  or or_8 (or_8_out, multiplexer_2_out, multiplexer_3_out);
  Multiplexer multiplexer_4 (.in0(multiplexer_1_out), .in1(multiplexer_3_out), .out(multiplexer_4_out), .sel(or_8_out));
  not not_2 (not_3_out[1], or_8_out);
  not not_3 (not_3_out[0], multiplexer_4_out);
  Multiplexer #(.width(4)) multiplexer_5 (.in0(4'b1000), .in1({1'b0, not_3_out}), .out(count), .sel(or_7_out));
  not not_4 (all_z, or_7_out);
endmodule

module CTZ_16bit (
  input  [15:0] A,
  output [4:0] count,
  output all_z
);

  wire Hi_all_z, Lo_all_z;
  wire [3:0] Hi_count, Lo_count;
  wire [3:3] not_1_out;

  CTZ_8bit Lo (.A(A[7:0]), .count(Lo_count), .all_z(Lo_all_z));
  CTZ_8bit Hi (.A(A[15:8]), .count(Hi_count), .all_z(Hi_all_z));
  and and_1 (all_z, Lo_all_z, Hi_all_z);
  not not_1 (not_1_out[3], Hi_count[3]);
  Multiplexer #(.width(5)) multiplexer_1 (
    .in0({1'b0, Lo_count}), .in1({Hi_count[3], not_1_out[3], Hi_count[2:0]}), .out(count), .sel(Lo_all_z));
endmodule

module CTZ_32bit (
  input  [31:0] A,
  output [5:0] count,
  output all_z
);

  wire Hi_all_z, Lo_all_z;
  wire [4:0] Hi_count, Lo_count;
  wire [4:4] not_1_out;

  CTZ_16bit Lo (.A(A[15:0]), .count(Lo_count), .all_z(Lo_all_z));
  CTZ_16bit Hi (.A(A[31:16]), .count(Hi_count), .all_z(Hi_all_z));
  and and_1 (all_z, Lo_all_z, Hi_all_z);
  not not_1 (not_1_out[4], Hi_count[4]);
  Multiplexer #(.width(6)) multiplexer_1 (
    .in0({1'b0, Lo_count}), .in1({Hi_count[4], not_1_out[4], Hi_count[3:0]}), .out(count), .sel(Lo_all_z));
endmodule

module correction (
  input  [31:0] A,
  input  [1:0] opcode,
  output [31:0] fixed
);

  wire [31:0] multiplexer_1_out, not_1_out;

  Multiplexer #(.width(32)) multiplexer_1 (.in0(A), .in1(not_1_out), .out(multiplexer_1_out), .sel(opcode[0]));
  assign not_1_out = ~A;  // NOT_Gate not_1, 32 bits wide
  Multiplexer #(.width(32)) multiplexer_2 (
    .in0(multiplexer_1_out),
    .in1({multiplexer_1_out[0], multiplexer_1_out[1], multiplexer_1_out[2], multiplexer_1_out[3], multiplexer_1_out[4], multiplexer_1_out[5], multiplexer_1_out[6], multiplexer_1_out[7], multiplexer_1_out[8], multiplexer_1_out[9], multiplexer_1_out[10], multiplexer_1_out[11], multiplexer_1_out[12], multiplexer_1_out[13], multiplexer_1_out[14], multiplexer_1_out[15], multiplexer_1_out[16], multiplexer_1_out[17], multiplexer_1_out[18], multiplexer_1_out[19], multiplexer_1_out[20], multiplexer_1_out[21], multiplexer_1_out[22], multiplexer_1_out[23], multiplexer_1_out[24], multiplexer_1_out[25], multiplexer_1_out[26], multiplexer_1_out[27], multiplexer_1_out[28], multiplexer_1_out[29], multiplexer_1_out[30], multiplexer_1_out[31]}),
    .out(fixed), .sel(opcode[1]));
endmodule
