// Logisim project HW3_403106238.circ as structural Verilog: 4 circuits, main circuit main
module main (
  input  [31:0] A,
  input  [31:0] B,
  input  Start,
  input  Clk,
  input  Rst,
  input  Divide,
  output [31:0] Result_Lo,
  output [31:0] Result_Hi,
  output Done
);

  wire ctrl_ld, ctrl_we;
  wire [63:0] div_unit_result, mul_unit_result;

  ctrl_unit ctrl (.Start(Start), .Clk(Clk), .Rst(Rst), .ld(ctrl_ld), .WE(ctrl_we), .Done(Done));
  mul mul_unit (.A(A), .B(B), .WE(ctrl_we), .Clk(Clk), .Rst(Rst), .ld(ctrl_ld), .Result(mul_unit_result));
  div div_unit (.A(A), .B(B), .WE(ctrl_we), .Clk(Clk), .Rst(Rst), .ld(ctrl_ld), .Result(div_unit_result));
  Multiplexer #(.width(64)) multiplexer_1 (
    .in0(mul_unit_result), .in1(div_unit_result), .out({Result_Hi, Result_Lo}), .sel(Divide));
endmodule

module mul (
  input  [31:0] A,
  input  [31:0] B,
  input  WE,
  input  Clk,
  input  Rst,
  input  ld,
  output [63:0] Result
);

  wire not_1_out;
  wire [31:0] adder_1_out;
  wire [32:0] multiplexer_2_out;
  wire [32:32] adder_1_cout;
  wire [63:0] multiplexer_1_out;

  Register #(.width(64)) register_1 (.D(multiplexer_1_out), .en(WE), .clk(Clk), .Q(Result), .clr(Rst));
  Multiplexer #(.width(64)) multiplexer_1 (
    .in0({multiplexer_2_out, Result[31:1]}), .in1({{32{1'b0}}, B}), .out(multiplexer_1_out), .sel(ld));
  Adder #(.width(32)) adder_1 (.a(A), .b(Result[63:32]), .out(adder_1_out), .cout(adder_1_cout[32]));  // open: cin
  Multiplexer #(.width(33)) multiplexer_2 (
    .in0({adder_1_cout[32], adder_1_out}), .in1({1'b0, Result[63:32]}), .out(multiplexer_2_out),
    .sel(not_1_out));
  not not_1 (not_1_out, Result[0]);
endmodule

module div (
  input  [31:0] A,
  input  [31:0] B,
  input  WE,
  input  Clk,
  input  Rst,
  input  ld,
  output [63:0] Result
);

  wire not_2_out;
  wire [0:0] adder_1_cout;
  wire [31:0] adder_1_out, multiplexer_2_out, not_1_out;
  wire [63:0] multiplexer_1_out;

  Register #(.width(64)) register_1 (.D(multiplexer_1_out), .en(WE), .clk(Clk), .Q(Result), .clr(Rst));
  Multiplexer #(.width(64)) multiplexer_1 (
    .in0({multiplexer_2_out, Result[30:0], adder_1_cout[0]}), .in1({{32{1'b0}}, A}), .out(multiplexer_1_out),
    .sel(ld));
  Adder #(.width(32)) adder_1 (.a(Result[62:31]), .b(not_1_out), .out(adder_1_out), .cin(1'b1), .cout(adder_1_cout[0]));
  assign not_1_out = ~B;  // NOT_Gate not_1, 32 bits wide
  Multiplexer #(.width(32)) multiplexer_2 (
    .in0(adder_1_out), .in1(Result[62:31]), .out(multiplexer_2_out), .sel(not_2_out));
  not not_2 (not_2_out, adder_1_cout[0]);
endmodule

module ctrl_unit (
  input  Start,
  input  Clk,
  input  Rst,
  output ld,
  output WE,
  output Done
);

  wire not_1_out;
  wire [1:0] multiplexer_2_out, register_1_q;
  wire [5:0] adder_1_out, multiplexer_3_out, register_2_q;

  Register #(.width(2)) register_1 (.D(multiplexer_2_out), .en(1'b1), .clk(Clk), .Q(register_1_q), .clr(Rst));
  Register #(.width(6)) register_2 (.D(multiplexer_3_out), .en(WE), .clk(Clk), .Q(register_2_q), .clr(Rst));
  not not_1 (not_1_out, Start);
  // Multiplexer #(.select(2)) multiplexer_1: pin names not known; wires that end beside it: 1'b0, 1'b1, 1'b1, multiplexer_2_out[1], not_1_out, register_1_q
  Adder #(.width(6)) adder_1 (.a(register_2_q), .b(6'b000001), .out(adder_1_out), .cin(1'b0));  // open: cout
  Multiplexer #(.select(2)) multiplexer_2 (
    .in0(Start), .in1(1'b0), .in2(register_2_q[5]), .in3(1'b1), .out(multiplexer_2_out[0]));  // open: sel
  Multiplexer #(.width(6)) multiplexer_3 (.in0(adder_1_out), .in1(6'b000001), .out(multiplexer_3_out), .sel(ld));
  and and_1 (ld, ~register_1_q[1], register_1_q[0]);  // AND_Gate
  xor xor_1 (WE, register_1_q[1], register_1_q[0]);
  and and_2 (Done, register_1_q[1], register_1_q[0]);
endmodule
