// Logisim project HW4_403106238.circ as structural Verilog: 9 circuits, main circuit main
module main (
  input  [31:0] A,
  input  [31:0] B,
  input  Sub,
  input  Clk,
  input  Rst,
  input  Start,
  output [31:0] Result,
  output Done
);

  wire ctrl_unit_1_en_align, ctrl_unit_1_en_e_work, ctrl_unit_1_en_m_work, ctrl_unit_1_en_s_res,
       ctrl_unit_1_load_regs, ctrl_unit_1_sel_e_work, datapath_1_exception, datapath_1_exp_eq,
       datapath_1_need_left, datapath_1_need_right, datapath_1_round_unnorm;
  wire [1:0] ctrl_unit_1_sel_m_work;

  Ctrl_Unit ctrl_unit_1 (
    .Clk(Clk), .Rst(Rst), .Start(Start), .exp_eq(datapath_1_exp_eq), .need_right(datapath_1_need_right),
    .need_left(datapath_1_need_left), .exception(datapath_1_exception),
    .round_unnorm(datapath_1_round_unnorm), .load_regs(ctrl_unit_1_load_regs),
    .en_align(ctrl_unit_1_en_align), .en_E_work(ctrl_unit_1_en_e_work), .sel_E_work(ctrl_unit_1_sel_e_work),
    .en_M_work(ctrl_unit_1_en_m_work), .sel_M_work(ctrl_unit_1_sel_m_work), .en_S_res(ctrl_unit_1_en_s_res),
    .Done(Done));
  Datapath datapath_1 (
    .A(A), .B(B), .Sub(Sub), .Clk(Clk), .Rst(Rst), .load_regs(ctrl_unit_1_load_regs),
    .en_align(ctrl_unit_1_en_align), .en_E_work(ctrl_unit_1_en_e_work), .sel_E_work(ctrl_unit_1_sel_e_work),
    .en_M_work(ctrl_unit_1_en_m_work), .sel_M_work(ctrl_unit_1_sel_m_work), .en_S_res(ctrl_unit_1_en_s_res),
    .exp_eq(datapath_1_exp_eq), .need_right(datapath_1_need_right), .need_left(datapath_1_need_left),
    .Result(Result), .exception(datapath_1_exception), .round_unnorm(datapath_1_round_unnorm));
endmodule

module Exp_Sub (
  input  [7:0] Ea,
  input  [7:0] Eb,
  output [7:0] diff,
  output a_larger,
  output exp_eq
);

  wire comparator_1_lt;
  wire [7:0] adder_1_out, adder_2_out, not_1_out, not_2_out;

  assign not_1_out = ~Eb;  // NOT_Gate not_1, 8 bits wide
  assign not_2_out = ~Ea;  // NOT_Gate not_2, 8 bits wide
  Comparator #(.mode("unsigned")) comparator_1 (.a(Ea), .b(Eb), .eq(exp_eq), .lt(comparator_1_lt));  // open: gt
  Adder adder_1 (.a(Ea), .b(not_1_out), .out(adder_1_out), .cin(1'b1));  // open: cout
  Adder adder_2 (.a(Eb), .b(not_2_out), .out(adder_2_out), .cin(1'b1));  // open: cout
  Multiplexer #(.width(8)) multiplexer_1 (.in0(adder_1_out), .in1(adder_2_out), .out(diff), .sel(comparator_1_lt));
  not not_3 (a_larger, comparator_1_lt);
endmodule

module Mantissa_Shift (
  input  [26:0] A,
  input  [7:0] Shift_Amt,
  output [26:0] SA
);

  wire comparator_1_lt;
  wire [31:0] barrel_shifter_1_result, bit_extender_1_out;

  assign bit_extender_1_out = {{5{1'b0}}, A};  // Bit_Extender bit_extender_1
  Comparator #(.mode("unsigned")) comparator_1 (.a(Shift_Amt), .b(8'h1b), .lt(comparator_1_lt));  // open: gt, eq
  Barrel_Shifter barrel_shifter_1 (
    .Data(bit_extender_1_out), .Shift_Op(2'b01), .Shift_Amt(Shift_Amt[4:0]), .Result(barrel_shifter_1_result));
  Multiplexer #(.width(27)) multiplexer_1 (
    .in0({27{1'b0}}), .in1(barrel_shifter_1_result[26:0]), .out(SA), .sel(comparator_1_lt));
endmodule

module Barrel_Shifter (
  input  [31:0] Data,
  input  [1:0] Shift_Op,
  input  [4:0] Shift_Amt,
  output [31:0] Result
);

  wire multiplexer_1_out, multiplexer_3_out, multiplexer_4_out, multiplexer_5_out, multiplexer_6_out,
       multiplexer_8_out, multiplexer_9_out, multiplexer_10_out, multiplexer_11_out, multiplexer_12_out,
       multiplexer_13_out, multiplexer_14_out, multiplexer_16_out, multiplexer_17_out, multiplexer_18_out,
       multiplexer_19_out, multiplexer_20_out, multiplexer_21_out, multiplexer_24_out, multiplexer_25_out,
       multiplexer_26_out, multiplexer_27_out, multiplexer_28_out, multiplexer_29_out, multiplexer_30_out,
       multiplexer_32_out, multiplexer_33_out, multiplexer_34_out, multiplexer_35_out, multiplexer_36_out,
       multiplexer_37_out, multiplexer_40_out, multiplexer_41_out, multiplexer_42_out, multiplexer_43_out,
       multiplexer_44_out, multiplexer_45_out, multiplexer_48_out, multiplexer_49_out, multiplexer_50_out,
       multiplexer_51_out, multiplexer_52_out, multiplexer_53_out, multiplexer_54_out, multiplexer_56_out,
       multiplexer_57_out, multiplexer_58_out, multiplexer_59_out, multiplexer_60_out, multiplexer_61_out,
       multiplexer_64_out, multiplexer_65_out, multiplexer_66_out, multiplexer_67_out, multiplexer_68_out,
       multiplexer_69_out, multiplexer_70_out, multiplexer_72_out, multiplexer_73_out, multiplexer_74_out,
       multiplexer_75_out, multiplexer_76_out, multiplexer_77_out, multiplexer_80_out, multiplexer_81_out,
       multiplexer_82_out, multiplexer_83_out, multiplexer_84_out, multiplexer_85_out, multiplexer_88_out,
       multiplexer_89_out, multiplexer_90_out, multiplexer_91_out, multiplexer_92_out, multiplexer_93_out,
       multiplexer_94_out, multiplexer_96_out, multiplexer_97_out, multiplexer_98_out, multiplexer_99_out,
       multiplexer_100_out, multiplexer_101_out, multiplexer_104_out, multiplexer_105_out,
       multiplexer_106_out, multiplexer_107_out, multiplexer_108_out, multiplexer_109_out,
       multiplexer_110_out, multiplexer_112_out, multiplexer_113_out, multiplexer_114_out,
       multiplexer_115_out, multiplexer_116_out, multiplexer_117_out, multiplexer_120_out,
       multiplexer_121_out, multiplexer_122_out, multiplexer_123_out, multiplexer_124_out,
       multiplexer_125_out, multiplexer_128_out, multiplexer_129_out, multiplexer_130_out,
       multiplexer_131_out, multiplexer_132_out, multiplexer_133_out, multiplexer_134_out,
       multiplexer_136_out, multiplexer_137_out, multiplexer_138_out, multiplexer_139_out,
       multiplexer_140_out, multiplexer_141_out, multiplexer_144_out, multiplexer_145_out,
       multiplexer_146_out, multiplexer_147_out, multiplexer_148_out, multiplexer_149_out,
       multiplexer_150_out, multiplexer_152_out, multiplexer_153_out, multiplexer_154_out,
       multiplexer_155_out, multiplexer_156_out, multiplexer_157_out, multiplexer_160_out,
       multiplexer_161_out, nor_1_out;
  wire [31:0] multiplexer_2_out, multiplexer_7_out;

  nor nor_1 (nor_1_out, Shift_Op[0], Shift_Op[1]);
  Multiplexer multiplexer_1 (.in0(1'b0), .in1(Data[31]), .out(multiplexer_1_out), .sel(Shift_Op[1]));
  Multiplexer #(.width(32)) multiplexer_2 (
    .in0(Data),
    .in1({Data[0], Data[1], Data[2], Data[3], Data[4], Data[5], Data[6], Data[7], Data[8], Data[9], Data[10], Data[11], Data[12], Data[13], Data[14], Data[15], Data[16], Data[17], Data[18], Data[19], Data[20], Data[21], Data[22], Data[23], Data[24], Data[25], Data[26], Data[27], Data[28], Data[29], Data[30], Data[31]}),
    .out(multiplexer_2_out), .sel(nor_1_out));
  Multiplexer multiplexer_3 (
    .in0(multiplexer_2_out[31]), .in1(multiplexer_1_out), .out(multiplexer_3_out), .sel(Shift_Amt[4]));
  Multiplexer multiplexer_4 (
    .in0(multiplexer_3_out), .in1(multiplexer_1_out), .out(multiplexer_4_out), .sel(Shift_Amt[3]));
  Multiplexer multiplexer_5 (
    .in0(multiplexer_4_out), .in1(multiplexer_1_out), .out(multiplexer_5_out), .sel(Shift_Amt[2]));
  Multiplexer multiplexer_6 (
    .in0(multiplexer_5_out), .in1(multiplexer_1_out), .out(multiplexer_6_out), .sel(Shift_Amt[1]));
  Multiplexer multiplexer_7 (
    .in0(multiplexer_6_out), .in1(multiplexer_1_out), .out(multiplexer_7_out[0]), .sel(Shift_Amt[0]));
  Multiplexer multiplexer_8 (
    .in0(multiplexer_2_out[30]), .in1(multiplexer_1_out), .out(multiplexer_8_out), .sel(Shift_Amt[4]));
  Multiplexer multiplexer_9 (
    .in0(multiplexer_2_out[29]), .in1(multiplexer_1_out), .out(multiplexer_9_out), .sel(Shift_Amt[4]));
  Multiplexer multiplexer_10 (
    .in0(multiplexer_8_out), .in1(multiplexer_1_out), .out(multiplexer_10_out), .sel(Shift_Amt[3]));
  Multiplexer multiplexer_11 (
    .in0(multiplexer_9_out), .in1(multiplexer_1_out), .out(multiplexer_11_out), .sel(Shift_Amt[3]));
  Multiplexer multiplexer_12 (
    .in0(multiplexer_10_out), .in1(multiplexer_1_out), .out(multiplexer_12_out), .sel(Shift_Amt[2]));
  Multiplexer multiplexer_13 (
    .in0(multiplexer_11_out), .in1(multiplexer_1_out), .out(multiplexer_13_out), .sel(Shift_Amt[2]));
  Multiplexer multiplexer_14 (
    .in0(multiplexer_12_out), .in1(multiplexer_1_out), .out(multiplexer_14_out), .sel(Shift_Amt[1]));
  Multiplexer multiplexer_15 (
    .in0(multiplexer_14_out), .in1(multiplexer_6_out), .out(multiplexer_7_out[1]), .sel(Shift_Amt[0]));
  Multiplexer multiplexer_16 (
    .in0(multiplexer_2_out[28]), .in1(multiplexer_1_out), .out(multiplexer_16_out), .sel(Shift_Amt[4]));
  Multiplexer multiplexer_17 (
    .in0(multiplexer_2_out[27]), .in1(multiplexer_1_out), .out(multiplexer_17_out), .sel(Shift_Amt[4]));
  Multiplexer multiplexer_18 (
    .in0(multiplexer_16_out), .in1(multiplexer_1_out), .out(multiplexer_18_out), .sel(Shift_Amt[3]));
  Multiplexer multiplexer_19 (
    .in0(multiplexer_18_out), .in1(multiplexer_1_out), .out(multiplexer_19_out), .sel(Shift_Amt[2]));
  Multiplexer multiplexer_20 (
    .in0(multiplexer_13_out), .in1(multiplexer_5_out), .out(multiplexer_20_out), .sel(Shift_Amt[1]));
  Multiplexer multiplexer_21 (
    .in0(multiplexer_19_out), .in1(multiplexer_12_out), .out(multiplexer_21_out), .sel(Shift_Amt[1]));
  Multiplexer multiplexer_22 (
    .in0(multiplexer_20_out), .in1(multiplexer_14_out), .out(multiplexer_7_out[2]), .sel(Shift_Amt[0]));
  Multiplexer multiplexer_23 (
    .in0(multiplexer_21_out), .in1(multiplexer_20_out), .out(multiplexer_7_out[3]), .sel(Shift_Amt[0]));
  Multiplexer multiplexer_24 (
    .in0(multiplexer_2_out[26]), .in1(multiplexer_1_out), .out(multiplexer_24_out), .sel(Shift_Amt[4]));
  Multiplexer multiplexer_25 (
    .in0(multiplexer_17_out), .in1(multiplexer_1_out), .out(multiplexer_25_out), .sel(Shift_Amt[3]));
  Multiplexer multiplexer_26 (
    .in0(multiplexer_24_out), .in1(multiplexer_1_out), .out(multiplexer_26_out), .sel(Shift_Amt[3]));
  Multiplexer multiplexer_27 (
    .in0(multiplexer_25_out), .in1(multiplexer_4_out), .out(multiplexer_27_out), .sel(Shift_Amt[2]));
  Multiplexer multiplexer_28 (
    .in0(multiplexer_26_out), .in1(multiplexer_10_out), .out(multiplexer_28_out), .sel(Shift_Amt[2]));
  Multiplexer multiplexer_29 (
    .in0(multiplexer_27_out), .in1(multiplexer_13_out), .out(multiplexer_29_out), .sel(Shift_Amt[1]));
  Multiplexer multiplexer_30 (
    .in0(multiplexer_28_out), .in1(multiplexer_19_out), .out(multiplexer_30_out), .sel(Shift_Amt[1]));
  Multiplexer multiplexer_31 (
    .in0(multiplexer_29_out), .in1(multiplexer_21_out), .out(multiplexer_7_out[4]), .sel(Shift_Amt[0]));
  Multiplexer multiplexer_32 (
    .in0(multiplexer_2_out[25]), .in1(multiplexer_1_out), .out(multiplexer_32_out), .sel(Shift_Amt[4]));
  Multiplexer multiplexer_33 (
    .in0(multiplexer_2_out[24]), .in1(multiplexer_1_out), .out(multiplexer_33_out), .sel(Shift_Amt[4]));
  Multiplexer multiplexer_34 (
    .in0(multiplexer_32_out), .in1(multiplexer_1_out), .out(multiplexer_34_out), .sel(Shift_Amt[3]));
  Multiplexer multiplexer_35 (
    .in0(multiplexer_33_out), .in1(multiplexer_1_out), .out(multiplexer_35_out), .sel(Shift_Amt[3]));
  Multiplexer multiplexer_36 (
    .in0(multiplexer_34_out), .in1(multiplexer_11_out), .out(multiplexer_36_out), .sel(Shift_Amt[2]));
  Multiplexer multiplexer_37 (
    .in0(multiplexer_36_out), .in1(multiplexer_27_out), .out(multiplexer_37_out), .sel(Shift_Amt[1]));
  Multiplexer multiplexer_38 (
    .in0(multiplexer_30_out), .in1(multiplexer_29_out), .out(multiplexer_7_out[5]), .sel(Shift_Amt[0]));
  Multiplexer multiplexer_39 (
    .in0(multiplexer_37_out), .in1(multiplexer_30_out), .out(multiplexer_7_out[6]), .sel(Shift_Amt[0]));
  Multiplexer multiplexer_40 (
    .in0(multiplexer_2_out[23]), .in1(multiplexer_1_out), .out(multiplexer_40_out), .sel(Shift_Amt[4]));
  Multiplexer multiplexer_41 (
    .in0(multiplexer_40_out), .in1(multiplexer_3_out), .out(multiplexer_41_out), .sel(Shift_Amt[3]));
  Multiplexer multiplexer_42 (
    .in0(multiplexer_35_out), .in1(multiplexer_18_out), .out(multiplexer_42_out), .sel(Shift_Amt[2]));
  Multiplexer multiplexer_43 (
    .in0(multiplexer_41_out), .in1(multiplexer_25_out), .out(multiplexer_43_out), .sel(Shift_Amt[2]));
  Multiplexer multiplexer_44 (
    .in0(multiplexer_42_out), .in1(multiplexer_28_out), .out(multiplexer_44_out), .sel(Shift_Amt[1]));
  Multiplexer multiplexer_45 (
    .in0(multiplexer_43_out), .in1(multiplexer_36_out), .out(multiplexer_45_out), .sel(Shift_Amt[1]));
  Multiplexer multiplexer_46 (
    .in0(multiplexer_44_out), .in1(multiplexer_37_out), .out(multiplexer_7_out[7]), .sel(Shift_Amt[0]));
  Multiplexer multiplexer_47 (
    .in0(multiplexer_45_out), .in1(multiplexer_44_out), .out(multiplexer_7_out[8]), .sel(Shift_Amt[0]));
  Multiplexer multiplexer_48 (
    .in0(multiplexer_2_out[22]), .in1(multiplexer_1_out), .out(multiplexer_48_out), .sel(Shift_Amt[4]));
  Multiplexer multiplexer_49 (
    .in0(multiplexer_2_out[21]), .in1(multiplexer_1_out), .out(multiplexer_49_out), .sel(Shift_Amt[4]));
  Multiplexer multiplexer_50 (
    .in0(multiplexer_48_out), .in1(multiplexer_8_out), .out(multiplexer_50_out), .sel(Shift_Amt[3]));
  Multiplexer multiplexer_51 (
    .in0(multiplexer_49_out), .in1(multiplexer_9_out), .out(multiplexer_51_out), .sel(Shift_Amt[3]));
  Multiplexer multiplexer_52 (
    .in0(multiplexer_50_out), .in1(multiplexer_26_out), .out(multiplexer_52_out), .sel(Shift_Amt[2]));
  Multiplexer multiplexer_53 (
    .in0(multiplexer_51_out), .in1(multiplexer_34_out), .out(multiplexer_53_out), .sel(Shift_Amt[2]));
  Multiplexer multiplexer_54 (
    .in0(multiplexer_52_out), .in1(multiplexer_42_out), .out(multiplexer_54_out), .sel(Shift_Amt[1]));
  Multiplexer multiplexer_55 (
    .in0(multiplexer_54_out), .in1(multiplexer_45_out), .out(multiplexer_7_out[9]), .sel(Shift_Amt[0]));
  Multiplexer multiplexer_56 (
    .in0(multiplexer_2_out[20]), .in1(multiplexer_1_out), .out(multiplexer_56_out), .sel(Shift_Amt[4]));
  Multiplexer multiplexer_57 (
    .in0(multiplexer_2_out[19]), .in1(multiplexer_1_out), .out(multiplexer_57_out), .sel(Shift_Amt[4]));
  Multiplexer multiplexer_58 (
    .in0(multiplexer_56_out), .in1(multiplexer_16_out), .out(multiplexer_58_out), .sel(Shift_Amt[3]));
  Multiplexer multiplexer_59 (
    .in0(multiplexer_58_out), .in1(multiplexer_35_out), .out(multiplexer_59_out), .sel(Shift_Amt[2]));
  Multiplexer multiplexer_60 (
    .in0(multiplexer_53_out), .in1(multiplexer_43_out), .out(multiplexer_60_out), .sel(Shift_Amt[1]));
  Multiplexer multiplexer_61 (
    .in0(multiplexer_59_out), .in1(multiplexer_52_out), .out(multiplexer_61_out), .sel(Shift_Amt[1]));
  Multiplexer multiplexer_62 (
    .in0(multiplexer_60_out), .in1(multiplexer_54_out), .out(multiplexer_7_out[10]), .sel(Shift_Amt[0]));
  Multiplexer multiplexer_63 (
    .in0(multiplexer_61_out), .in1(multiplexer_60_out), .out(multiplexer_7_out[11]), .sel(Shift_Amt[0]));
  Multiplexer multiplexer_64 (
    .in0(multiplexer_2_out[18]), .in1(multiplexer_1_out), .out(multiplexer_64_out), .sel(Shift_Amt[4]));
  Multiplexer multiplexer_65 (
    .in0(multiplexer_64_out), .in1(multiplexer_24_out), .out(multiplexer_65_out), .sel(Shift_Amt[3]));
  Multiplexer multiplexer_66 (
    .in0(multiplexer_57_out), .in1(multiplexer_17_out), .out(multiplexer_66_out), .sel(Shift_Amt[3]));
  Multiplexer multiplexer_67 (
    .in0(multiplexer_65_out), .in1(multiplexer_50_out), .out(multiplexer_67_out), .sel(Shift_Amt[2]));
  Multiplexer multiplexer_68 (
    .in0(multiplexer_66_out), .in1(multiplexer_41_out), .out(multiplexer_68_out), .sel(Shift_Amt[2]));
  Multiplexer multiplexer_69 (
    .in0(multiplexer_67_out), .in1(multiplexer_59_out), .out(multiplexer_69_out), .sel(Shift_Amt[1]));
  Multiplexer multiplexer_70 (
    .in0(multiplexer_68_out), .in1(multiplexer_53_out), .out(multiplexer_70_out), .sel(Shift_Amt[1]));
  Multiplexer multiplexer_71 (
    .in0(multiplexer_70_out), .in1(multiplexer_61_out), .out(multiplexer_7_out[12]), .sel(Shift_Amt[0]));
  Multiplexer multiplexer_72 (
    .in0(multiplexer_2_out[17]), .in1(multiplexer_1_out), .out(multiplexer_72_out), .sel(Shift_Amt[4]));
  Multiplexer multiplexer_73 (
    .in0(multiplexer_2_out[16]), .in1(multiplexer_1_out), .out(multiplexer_73_out), .sel(Shift_Amt[4]));
  Multiplexer multiplexer_74 (
    .in0(multiplexer_72_out), .in1(multiplexer_32_out), .out(multiplexer_74_out), .sel(Shift_Amt[3]));
  Multiplexer multiplexer_75 (
    .in0(multiplexer_73_out), .in1(multiplexer_33_out), .out(multiplexer_75_out), .sel(Shift_Amt[3]));
  Multiplexer multiplexer_76 (
    .in0(multiplexer_74_out), .in1(multiplexer_51_out), .out(multiplexer_76_out), .sel(Shift_Amt[2]));
  Multiplexer multiplexer_77 (
    .in0(multiplexer_76_out), .in1(multiplexer_68_out), .out(multiplexer_77_out), .sel(Shift_Amt[1]));
  Multiplexer multiplexer_78 (
    .in0(multiplexer_69_out), .in1(multiplexer_70_out), .out(multiplexer_7_out[13]), .sel(Shift_Amt[0]));
  Multiplexer multiplexer_79 (
    .in0(multiplexer_77_out), .in1(multiplexer_69_out), .out(multiplexer_7_out[14]), .sel(Shift_Amt[0]));
  Multiplexer multiplexer_80 (
    .in0(multiplexer_2_out[15]), .in1(multiplexer_2_out[31]), .out(multiplexer_80_out), .sel(Shift_Amt[4]));
  Multiplexer multiplexer_81 (
    .in0(multiplexer_80_out), .in1(multiplexer_40_out), .out(multiplexer_81_out), .sel(Shift_Amt[3]));
  Multiplexer multiplexer_82 (
    .in0(multiplexer_75_out), .in1(multiplexer_58_out), .out(multiplexer_82_out), .sel(Shift_Amt[2]));
  Multiplexer multiplexer_83 (
    .in0(multiplexer_81_out), .in1(multiplexer_66_out), .out(multiplexer_83_out), .sel(Shift_Amt[2]));
  Multiplexer multiplexer_84 (
    .in0(multiplexer_82_out), .in1(multiplexer_67_out), .out(multiplexer_84_out), .sel(Shift_Amt[1]));
  Multiplexer multiplexer_85 (
    .in0(multiplexer_83_out), .in1(multiplexer_76_out), .out(multiplexer_85_out), .sel(Shift_Amt[1]));
  Multiplexer multiplexer_86 (
    .in0(multiplexer_84_out), .in1(multiplexer_77_out), .out(multiplexer_7_out[15]), .sel(Shift_Amt[0]));
  Multiplexer multiplexer_87 (
    .in0(multiplexer_85_out), .in1(multiplexer_84_out), .out(multiplexer_7_out[16]), .sel(Shift_Amt[0]));
  Multiplexer multiplexer_88 (
    .in0(multiplexer_2_out[14]), .in1(multiplexer_2_out[30]), .out(multiplexer_88_out), .sel(Shift_Amt[4]));
  Multiplexer multiplexer_89 (
    .in0(multiplexer_2_out[13]), .in1(multiplexer_2_out[29]), .out(multiplexer_89_out), .sel(Shift_Amt[4]));
  Multiplexer multiplexer_90 (
    .in0(multiplexer_88_out), .in1(multiplexer_48_out), .out(multiplexer_90_out), .sel(Shift_Amt[3]));
  Multiplexer multiplexer_91 (
    .in0(multiplexer_89_out), .in1(multiplexer_49_out), .out(multiplexer_91_out), .sel(Shift_Amt[3]));
  Multiplexer multiplexer_92 (
    .in0(multiplexer_90_out), .in1(multiplexer_65_out), .out(multiplexer_92_out), .sel(Shift_Amt[2]));
  Multiplexer multiplexer_93 (
    .in0(multiplexer_91_out), .in1(multiplexer_74_out), .out(multiplexer_93_out), .sel(Shift_Amt[2]));
  Multiplexer multiplexer_94 (
    .in0(multiplexer_92_out), .in1(multiplexer_82_out), .out(multiplexer_94_out), .sel(Shift_Amt[1]));
  Multiplexer multiplexer_95 (
    .in0(multiplexer_94_out), .in1(multiplexer_85_out), .out(multiplexer_7_out[17]), .sel(Shift_Amt[0]));
  Multiplexer multiplexer_96 (
    .in0(multiplexer_2_out[12]), .in1(multiplexer_2_out[28]), .out(multiplexer_96_out), .sel(Shift_Amt[4]));
  Multiplexer multiplexer_97 (
    .in0(multiplexer_2_out[11]), .in1(multiplexer_2_out[27]), .out(multiplexer_97_out), .sel(Shift_Amt[4]));
  Multiplexer multiplexer_98 (
    .in0(multiplexer_96_out), .in1(multiplexer_56_out), .out(multiplexer_98_out), .sel(Shift_Amt[3]));
  Multiplexer multiplexer_99 (
    .in0(multiplexer_98_out), .in1(multiplexer_75_out), .out(multiplexer_99_out), .sel(Shift_Amt[2]));
  Multiplexer multiplexer_100 (
    .in0(multiplexer_93_out), .in1(multiplexer_83_out), .out(multiplexer_100_out), .sel(Shift_Amt[1]));
  Multiplexer multiplexer_101 (
    .in0(multiplexer_99_out), .in1(multiplexer_92_out), .out(multiplexer_101_out), .sel(Shift_Amt[1]));
  Multiplexer multiplexer_102 (
    .in0(multiplexer_100_out), .in1(multiplexer_94_out), .out(multiplexer_7_out[18]), .sel(Shift_Amt[0]));
  Multiplexer multiplexer_103 (
    .in0(multiplexer_101_out), .in1(multiplexer_100_out), .out(multiplexer_7_out[19]), .sel(Shift_Amt[0]));
  Multiplexer multiplexer_104 (
    .in0(multiplexer_2_out[10]), .in1(multiplexer_2_out[26]), .out(multiplexer_104_out), .sel(Shift_Amt[4]));
  Multiplexer multiplexer_105 (
    .in0(multiplexer_97_out), .in1(multiplexer_57_out), .out(multiplexer_105_out), .sel(Shift_Amt[3]));
  Multiplexer multiplexer_106 (
    .in0(multiplexer_104_out), .in1(multiplexer_64_out), .out(multiplexer_106_out), .sel(Shift_Amt[3]));
  Multiplexer multiplexer_107 (
    .in0(multiplexer_105_out), .in1(multiplexer_81_out), .out(multiplexer_107_out), .sel(Shift_Amt[2]));
  Multiplexer multiplexer_108 (
    .in0(multiplexer_106_out), .in1(multiplexer_90_out), .out(multiplexer_108_out), .sel(Shift_Amt[2]));
  Multiplexer multiplexer_109 (
    .in0(multiplexer_107_out), .in1(multiplexer_93_out), .out(multiplexer_109_out), .sel(Shift_Amt[1]));
  Multiplexer multiplexer_110 (
    .in0(multiplexer_108_out), .in1(multiplexer_99_out), .out(multiplexer_110_out), .sel(Shift_Amt[1]));
  Multiplexer multiplexer_111 (
    .in0(multiplexer_109_out), .in1(multiplexer_101_out), .out(multiplexer_7_out[20]), .sel(Shift_Amt[0]));
  Multiplexer multiplexer_112 (
    .in0(multiplexer_2_out[9]), .in1(multiplexer_2_out[25]), .out(multiplexer_112_out), .sel(Shift_Amt[4]));
  Multiplexer multiplexer_113 (
    .in0(multiplexer_2_out[8]), .in1(multiplexer_2_out[24]), .out(multiplexer_113_out), .sel(Shift_Amt[4]));
  Multiplexer multiplexer_114 (
    .in0(multiplexer_112_out), .in1(multiplexer_72_out), .out(multiplexer_114_out), .sel(Shift_Amt[3]));
  Multiplexer multiplexer_115 (
    .in0(multiplexer_113_out), .in1(multiplexer_73_out), .out(multiplexer_115_out), .sel(Shift_Amt[3]));
  Multiplexer multiplexer_116 (
    .in0(multiplexer_114_out), .in1(multiplexer_91_out), .out(multiplexer_116_out), .sel(Shift_Amt[2]));
  Multiplexer multiplexer_117 (
    .in0(multiplexer_116_out), .in1(multiplexer_107_out), .out(multiplexer_117_out), .sel(Shift_Amt[1]));
  Multiplexer multiplexer_118 (
    .in0(multiplexer_110_out), .in1(multiplexer_109_out), .out(multiplexer_7_out[21]), .sel(Shift_Amt[0]));
  Multiplexer multiplexer_119 (
    .in0(multiplexer_117_out), .in1(multiplexer_110_out), .out(multiplexer_7_out[22]), .sel(Shift_Amt[0]));
  Multiplexer multiplexer_120 (
    .in0(multiplexer_2_out[7]), .in1(multiplexer_2_out[23]), .out(multiplexer_120_out), .sel(Shift_Amt[4]));
  Multiplexer multiplexer_121 (
    .in0(multiplexer_120_out), .in1(multiplexer_80_out), .out(multiplexer_121_out), .sel(Shift_Amt[3]));
  Multiplexer multiplexer_122 (
    .in0(multiplexer_115_out), .in1(multiplexer_98_out), .out(multiplexer_122_out), .sel(Shift_Amt[2]));
  Multiplexer multiplexer_123 (
    .in0(multiplexer_121_out), .in1(multiplexer_105_out), .out(multiplexer_123_out), .sel(Shift_Amt[2]));
  Multiplexer multiplexer_124 (
    .in0(multiplexer_122_out), .in1(multiplexer_108_out), .out(multiplexer_124_out), .sel(Shift_Amt[1]));
  Multiplexer multiplexer_125 (
    .in0(multiplexer_123_out), .in1(multiplexer_116_out), .out(multiplexer_125_out), .sel(Shift_Amt[1]));
  Multiplexer multiplexer_126 (
    .in0(multiplexer_124_out), .in1(multiplexer_117_out), .out(multiplexer_7_out[23]), .sel(Shift_Amt[0]));
  Multiplexer multiplexer_127 (
    .in0(multiplexer_125_out), .in1(multiplexer_124_out), .out(multiplexer_7_out[24]), .sel(Shift_Amt[0]));
  Multiplexer multiplexer_128 (
    .in0(multiplexer_2_out[6]), .in1(multiplexer_2_out[22]), .out(multiplexer_128_out), .sel(Shift_Amt[4]));
  Multiplexer multiplexer_129 (
    .in0(multiplexer_2_out[5]), .in1(multiplexer_2_out[21]), .out(multiplexer_129_out), .sel(Shift_Amt[4]));
  Multiplexer multiplexer_130 (
    .in0(multiplexer_128_out), .in1(multiplexer_88_out), .out(multiplexer_130_out), .sel(Shift_Amt[3]));
  Multiplexer multiplexer_131 (
    .in0(multiplexer_129_out), .in1(multiplexer_89_out), .out(multiplexer_131_out), .sel(Shift_Amt[3]));
  Multiplexer multiplexer_132 (
    .in0(multiplexer_130_out), .in1(multiplexer_106_out), .out(multiplexer_132_out), .sel(Shift_Amt[2]));
  Multiplexer multiplexer_133 (
    .in0(multiplexer_131_out), .in1(multiplexer_114_out), .out(multiplexer_133_out), .sel(Shift_Amt[2]));
  Multiplexer multiplexer_134 (
    .in0(multiplexer_132_out), .in1(multiplexer_122_out), .out(multiplexer_134_out), .sel(Shift_Amt[1]));
  Multiplexer multiplexer_135 (
    .in0(multiplexer_134_out), .in1(multiplexer_125_out), .out(multiplexer_7_out[25]), .sel(Shift_Amt[0]));
  Multiplexer multiplexer_136 (
    .in0(multiplexer_2_out[4]), .in1(multiplexer_2_out[20]), .out(multiplexer_136_out), .sel(Shift_Amt[4]));
  Multiplexer multiplexer_137 (
    .in0(multiplexer_2_out[3]), .in1(multiplexer_2_out[19]), .out(multiplexer_137_out), .sel(Shift_Amt[4]));
  Multiplexer multiplexer_138 (
    .in0(multiplexer_136_out), .in1(multiplexer_96_out), .out(multiplexer_138_out), .sel(Shift_Amt[3]));
  Multiplexer multiplexer_139 (
    .in0(multiplexer_138_out), .in1(multiplexer_115_out), .out(multiplexer_139_out), .sel(Shift_Amt[2]));
  Multiplexer multiplexer_140 (
    .in0(multiplexer_133_out), .in1(multiplexer_123_out), .out(multiplexer_140_out), .sel(Shift_Amt[1]));
  Multiplexer multiplexer_141 (
    .in0(multiplexer_139_out), .in1(multiplexer_132_out), .out(multiplexer_141_out), .sel(Shift_Amt[1]));
  Multiplexer multiplexer_142 (
    .in0(multiplexer_140_out), .in1(multiplexer_134_out), .out(multiplexer_7_out[26]), .sel(Shift_Amt[0]));
  Multiplexer multiplexer_143 (
    .in0(multiplexer_141_out), .in1(multiplexer_140_out), .out(multiplexer_7_out[27]), .sel(Shift_Amt[0]));
  Multiplexer multiplexer_144 (
    .in0(multiplexer_2_out[2]), .in1(multiplexer_2_out[18]), .out(multiplexer_144_out), .sel(Shift_Amt[4]));
  Multiplexer multiplexer_145 (
    .in0(multiplexer_137_out), .in1(multiplexer_97_out), .out(multiplexer_145_out), .sel(Shift_Amt[3]));
  Multiplexer multiplexer_146 (
    .in0(multiplexer_144_out), .in1(multiplexer_104_out), .out(multiplexer_146_out), .sel(Shift_Amt[3]));
  Multiplexer multiplexer_147 (
    .in0(multiplexer_145_out), .in1(multiplexer_121_out), .out(multiplexer_147_out), .sel(Shift_Amt[2]));
  Multiplexer multiplexer_148 (
    .in0(multiplexer_146_out), .in1(multiplexer_130_out), .out(multiplexer_148_out), .sel(Shift_Amt[2]));
  Multiplexer multiplexer_149 (
    .in0(multiplexer_147_out), .in1(multiplexer_133_out), .out(multiplexer_149_out), .sel(Shift_Amt[1]));
  Multiplexer multiplexer_150 (
    .in0(multiplexer_148_out), .in1(multiplexer_139_out), .out(multiplexer_150_out), .sel(Shift_Amt[1]));
  Multiplexer multiplexer_151 (
    .in0(multiplexer_149_out), .in1(multiplexer_141_out), .out(multiplexer_7_out[28]), .sel(Shift_Amt[0]));
  Multiplexer multiplexer_152 (
    .in0(multiplexer_2_out[1]), .in1(multiplexer_2_out[17]), .out(multiplexer_152_out), .sel(Shift_Amt[4]));
  Multiplexer multiplexer_153 (
    .in0(multiplexer_2_out[0]), .in1(multiplexer_2_out[16]), .out(multiplexer_153_out), .sel(Shift_Amt[4]));
  Multiplexer multiplexer_154 (
    .in0(multiplexer_152_out), .in1(multiplexer_112_out), .out(multiplexer_154_out), .sel(Shift_Amt[3]));
  Multiplexer multiplexer_155 (
    .in0(multiplexer_153_out), .in1(multiplexer_113_out), .out(multiplexer_155_out), .sel(Shift_Amt[3]));
  Multiplexer multiplexer_156 (
    .in0(multiplexer_154_out), .in1(multiplexer_131_out), .out(multiplexer_156_out), .sel(Shift_Amt[2]));
  Multiplexer multiplexer_157 (
    .in0(multiplexer_156_out), .in1(multiplexer_147_out), .out(multiplexer_157_out), .sel(Shift_Amt[1]));
  Multiplexer multiplexer_158 (
    .in0(multiplexer_150_out), .in1(multiplexer_149_out), .out(multiplexer_7_out[29]), .sel(Shift_Amt[0]));
  Multiplexer multiplexer_159 (
    .in0(multiplexer_157_out), .in1(multiplexer_150_out), .out(multiplexer_7_out[30]), .sel(Shift_Amt[0]));
  Multiplexer multiplexer_160 (
    .in0(multiplexer_155_out), .in1(multiplexer_138_out), .out(multiplexer_160_out), .sel(Shift_Amt[2]));
  Multiplexer multiplexer_161 (
    .in0(multiplexer_160_out), .in1(multiplexer_148_out), .out(multiplexer_161_out), .sel(Shift_Amt[1]));
  Multiplexer multiplexer_162 (
    .in0(multiplexer_161_out), .in1(multiplexer_157_out), .out(multiplexer_7_out[31]), .sel(Shift_Amt[0]));
  Multiplexer #(.width(32)) multiplexer_163 (
    .in0({multiplexer_7_out[0], multiplexer_7_out[1], multiplexer_7_out[2], multiplexer_7_out[3], multiplexer_7_out[4], multiplexer_7_out[5], multiplexer_7_out[6], multiplexer_7_out[7], multiplexer_7_out[8], multiplexer_7_out[9], multiplexer_7_out[10], multiplexer_7_out[11], multiplexer_7_out[12], multiplexer_7_out[13], multiplexer_7_out[14], multiplexer_7_out[15], multiplexer_7_out[16], multiplexer_7_out[17], multiplexer_7_out[18], multiplexer_7_out[19], multiplexer_7_out[20], multiplexer_7_out[21], multiplexer_7_out[22], multiplexer_7_out[23], multiplexer_7_out[24], multiplexer_7_out[25], multiplexer_7_out[26], multiplexer_7_out[27], multiplexer_7_out[28], multiplexer_7_out[29], multiplexer_7_out[30], multiplexer_7_out[31]}),
    .in1(multiplexer_7_out), .out(Result), .sel(nor_1_out));
endmodule

module Big_ALU (
  input  [26:0] Ma,
  input  [26:0] Mb,
  input  Sa,
  input  Sb_eff,
  output [27:0] M_res,
  output overflow,
  output S_res
);

  wire comparator_1_lt, multiplexer_3_out, not_1_out, xor_1_out;
  wire [27:0] adder_1_out, adder_2_out, adder_3_out, bit_extender_1_out, bit_extender_2_out,
       multiplexer_1_out, not_2_out, not_3_out;

  xor xor_1 (xor_1_out, Sa, Sb_eff);
  Comparator #(.mode("unsigned"), .width(27)) comparator_1 (.a(Ma), .b(Mb), .lt(comparator_1_lt));  // open: gt, eq
  not not_1 (not_1_out, comparator_1_lt);
  assign bit_extender_1_out = {{1{1'b0}}, Ma};  // Bit_Extender bit_extender_1
  assign bit_extender_2_out = {{1{1'b0}}, Mb};  // Bit_Extender bit_extender_2
  Adder #(.width(28)) adder_1 (.a(bit_extender_1_out), .b(bit_extender_2_out), .out(adder_1_out));  // open: cin, cout
  Adder #(.width(28)) adder_2 (.a(bit_extender_1_out), .b(not_2_out), .out(adder_2_out), .cin(1'b1));  // open: cout
  assign not_2_out = ~bit_extender_2_out;  // NOT_Gate not_2, 28 bits wide
  Adder #(.width(28)) adder_3 (.a(bit_extender_2_out), .b(not_3_out), .out(adder_3_out), .cin(1'b1));  // open: cout
  assign not_3_out = ~bit_extender_1_out;  // NOT_Gate not_3, 28 bits wide
  Multiplexer #(.width(28)) multiplexer_1 (
    .in0(adder_3_out), .in1(adder_2_out), .out(multiplexer_1_out), .sel(not_1_out));
  Multiplexer #(.width(28)) multiplexer_2 (.in0(adder_1_out), .in1(multiplexer_1_out), .out(M_res), .sel(xor_1_out));
  Multiplexer multiplexer_3 (.in0(Sb_eff), .in1(Sa), .out(multiplexer_3_out), .sel(not_1_out));
  Multiplexer multiplexer_4 (.in0(Sa), .in1(multiplexer_3_out), .out(S_res), .sel(xor_1_out));

  assign overflow = M_res[27];
endmodule

module Normalizer (
  input  [27:0] M_in,
  input  [7:0] E_in,
  output need_right,
  output need_left,
  output [26:0] M_out,
  output [7:0] E_out,
  output exception
);

  wire and_2_out, comparator_1_gt, comparator_2_eq;
  wire [7:0] adder_1_out, adder_2_out, multiplexer_3_out, multiplexer_4_out, not_1_out;
  wire [26:0] multiplexer_1_out, multiplexer_2_out;

  assign not_1_out = ~8'h1;  // NOT_Gate not_1, 8 bits wide
  Comparator #(.mode("unsigned")) comparator_1 (.a(E_in), .b({8{1'b0}}), .gt(comparator_1_gt));  // open: eq, lt
  Adder adder_1 (.a(E_in), .b(8'h1), .out(adder_1_out));  // open: cin, cout
  Adder adder_2 (.a(E_in), .b(not_1_out), .out(adder_2_out), .cin(1'b1));  // open: cout
  Multiplexer #(.width(27)) multiplexer_1 (
    .in0(M_in[26:0]), .in1({M_in[25:0], 1'b0}), .out(multiplexer_1_out), .sel(need_left));
  Multiplexer #(.width(27)) multiplexer_2 (
    .in0(multiplexer_1_out), .in1(M_in[27:1]), .out(multiplexer_2_out), .sel(M_in[27]));
  Multiplexer #(.width(8)) multiplexer_3 (.in0(E_in), .in1(adder_2_out), .out(multiplexer_3_out), .sel(need_left));
  Multiplexer #(.width(8)) multiplexer_4 (
    .in0(multiplexer_3_out), .in1(adder_1_out), .out(multiplexer_4_out), .sel(M_in[27]));
  and and_1 (need_left, ~M_in[27], ~M_in[26], comparator_1_gt);  // AND_Gate
  Comparator #(.mode("unsigned")) comparator_2 (
    .a(multiplexer_4_out), .b({8{1'b0}}), .eq(comparator_2_eq));  // open: gt, lt
  Comparator #(.mode("unsigned")) comparator_3 (.a(multiplexer_4_out), .b({8{1'b1}}), .eq(exception));  // open: gt, lt
  Multiplexer #(.width(27)) multiplexer_5 (
    .in0(multiplexer_2_out), .in1({1'b0, M_in[25:0]}), .out(M_out), .sel(and_2_out));
  and and_2 (and_2_out, M_in[26], comparator_2_eq);
  Multiplexer #(.width(8)) multiplexer_6 (.in0(multiplexer_4_out), .in1(8'h1), .out(E_out), .sel(and_2_out));

  assign need_right = M_in[27];
endmodule

module Rounder (
  input  [26:0] M_in,
  output [22:0] fraction,
  output round_unnorm,
  output [27:0] M_fb
);

  wire and_1_out, or_1_out;

  or or_1 (or_1_out, M_in[0], M_in[1], M_in[3]);
  Adder #(.width(24)) adder_1 (
    .a(M_in[26:3]), .b({24{1'b0}}), .out({M_fb[26], fraction}), .cin(and_1_out), .cout(M_fb[27]));
  and and_1 (and_1_out, or_1_out, M_in[2]);

  assign M_fb[25:0] = {fraction, 3'b000};
  assign round_unnorm = M_fb[27];
endmodule

module Datapath (
  input  [31:0] A,
  input  [31:0] B,
  input  Sub,
  input  Clk,
  input  Rst,
  input  load_regs,
  input  en_align,
  input  en_E_work,
  input  sel_E_work,
  input  en_M_work,
  input  [1:0] sel_M_work,
  input  en_S_res,
  output exp_eq,
  output need_right,
  output need_left,
  output [31:0] Result,
  output exception,
  output round_unnorm
);

  wire and_1_out, and_2_out, and_3_out, big_alu_1_s_res, comparator_1_eq, comparator_2_eq,
       Exp_Sub_1_a_larger, or_1_out, or_2_out, Sa_reg_q, Sb_eff_reg_q, xor_1_out;
  wire [7:0] Ea_reg_q, Eb_reg_q, Exp_Sub_1_diff, multiplexer_2_out, multiplexer_3_out, multiplexer_4_out,
       multiplexer_7_out, MUX_E_align, normalizer_1_e_out;
  wire [26:0] Ma_reg_q, mantissa_shifter_sa, Mb_reg_q, multiplexer_1_out, multiplexer_5_out,
       multiplexer_8_out, normalizer_1_m_out;
  wire [26:26] not_1_out, not_2_out;
  wire [27:0] big_alu_1_m_res, M_work_reg_q, multiplexer_9_out, multiplexer_10_out, rounder_1_m_fb;

  not not_1 (not_1_out[26], comparator_1_eq);
  Comparator comparator_1 (.a(A[30:23]), .b({8{1'b0}}), .eq(comparator_1_eq));  // open: gt, lt
  and and_1 (and_1_out, en_align, ~Exp_Sub_1_a_larger);  // AND_Gate
  xor xor_1 (xor_1_out, B[31], Sub);
  not not_2 (not_2_out[26], comparator_2_eq);
  Comparator comparator_2 (.a(B[30:23]), .b({8{1'b0}}), .eq(comparator_2_eq));  // open: gt, lt
  and and_2 (and_2_out, comparator_1_eq, comparator_2_eq);
  Multiplexer #(.width(27)) multiplexer_1 (
    .in0({not_1_out[26], A[22:0], 3'b000}), .in1(mantissa_shifter_sa), .out(multiplexer_1_out), .sel(en_align));
  or or_1 (or_1_out, and_1_out, load_regs);
  Register #(.width(1)) S_res_reg (.D(big_alu_1_s_res), .en(en_S_res), .clk(Clk), .Q(Result[31]), .clr(Rst));
  Register E_work_reg (.D(multiplexer_2_out), .en(en_E_work), .clk(Clk), .Q(Result[30:23]), .clr(Rst));
  Multiplexer #(.width(8)) multiplexer_2 (
    .in0(MUX_E_align), .in1(normalizer_1_e_out), .out(multiplexer_2_out), .sel(sel_E_work));
  Register #(.width(1)) Sa_reg (.D(A[31]), .en(load_regs), .clk(Clk), .Q(Sa_reg_q), .clr(Rst));
  Multiplexer #(.width(8)) multiplexer_3 (.in0(A[30:23]), .in1(8'h1), .out(multiplexer_3_out), .sel(comparator_1_eq));
  Register Ea_reg (.D(multiplexer_3_out), .en(load_regs), .clk(Clk), .Q(Ea_reg_q), .clr(Rst));
  Register #(.width(27)) Ma_reg (.D(multiplexer_1_out), .en(or_1_out), .clk(Clk), .Q(Ma_reg_q), .clr(Rst));
  and and_3 (and_3_out, en_align, Exp_Sub_1_a_larger);
  Register #(.width(28)) M_work_reg (.D(multiplexer_10_out), .en(en_M_work), .clk(Clk), .Q(M_work_reg_q), .clr(Rst));
  Register #(.width(1)) Sb_eff_reg (.D(xor_1_out), .en(load_regs), .clk(Clk), .Q(Sb_eff_reg_q), .clr(Rst));
  Multiplexer #(.width(8)) multiplexer_4 (.in0(B[30:23]), .in1(8'h1), .out(multiplexer_4_out), .sel(comparator_2_eq));
  Register Eb_reg (.D(multiplexer_4_out), .en(load_regs), .clk(Clk), .Q(Eb_reg_q), .clr(Rst));
  Multiplexer #(.width(27)) multiplexer_5 (
    .in0({not_2_out[26], B[22:0], 3'b000}), .in1(mantissa_shifter_sa), .out(multiplexer_5_out), .sel(en_align));
  or or_2 (or_2_out, and_3_out, load_regs);
  Register #(.width(27)) Mb_reg (.D(multiplexer_5_out), .en(or_2_out), .clk(Clk), .Q(Mb_reg_q), .clr(Rst));
  Multiplexer #(.width(8)) multiplexer_6 (.in0(Eb_reg_q), .in1(Ea_reg_q), .out(MUX_E_align), .sel(Exp_Sub_1_a_larger));
  Big_ALU big_alu_1 (
    .Ma(Ma_reg_q), .Mb(Mb_reg_q), .Sa(Sa_reg_q), .Sb_eff(Sb_eff_reg_q), .M_res(big_alu_1_m_res),
    .S_res(big_alu_1_s_res));  // open: overflow
  Multiplexer #(.width(8)) multiplexer_7 (
    .in0(Result[30:23]), .in1({8{1'b0}}), .out(multiplexer_7_out), .sel(and_2_out));
  Multiplexer #(.width(27)) multiplexer_8 (
    .in0(Ma_reg_q), .in1(Mb_reg_q), .out(multiplexer_8_out), .sel(Exp_Sub_1_a_larger));
  Exp_Sub Exp_Sub_1 (
    .Ea(Ea_reg_q), .Eb(Eb_reg_q), .diff(Exp_Sub_1_diff), .a_larger(Exp_Sub_1_a_larger), .exp_eq(exp_eq));
  Multiplexer #(.width(28)) multiplexer_9 (
    .in0(big_alu_1_m_res), .in1({1'b0, normalizer_1_m_out}), .out(multiplexer_9_out), .sel(sel_M_work[0]));
  Multiplexer #(.width(28)) multiplexer_10 (
    .in0(multiplexer_9_out), .in1(rounder_1_m_fb), .out(multiplexer_10_out), .sel(sel_M_work[1]));
  Normalizer normalizer_1 (
    .M_in(M_work_reg_q), .E_in(multiplexer_7_out), .need_right(need_right), .need_left(need_left),
    .M_out(normalizer_1_m_out), .E_out(normalizer_1_e_out), .exception(exception));
  Rounder rounder_1 (
    .M_in(M_work_reg_q[26:0]), .fraction(Result[22:0]), .round_unnorm(round_unnorm), .M_fb(rounder_1_m_fb));
  Mantissa_Shift mantissa_shifter (.A(multiplexer_8_out), .Shift_Amt(Exp_Sub_1_diff), .SA(mantissa_shifter_sa));

  // Other names for the same wires on the sheet: lr = load_regs
endmodule

module Ctrl_Unit (
  input  Clk,
  input  Rst,
  input  Start,
  input  exp_eq,
  input  need_right,
  input  need_left,
  input  exception,
  input  round_unnorm,
  output load_regs,
  output en_align,
  output en_E_work,
  output sel_E_work,
  output en_M_work,
  output [1:0] sel_M_work,
  output en_S_res,
  output Done
);

  wire and_2_out, and_3_out, and_4_out, and_5_out, and_6_out, and_7_out, done_stay, is_IDLE, nor_1_out;
  wire [2:0] or_5_out, state_q;

  and and_1 (done_stay, ~Start, Done);  // AND_Gate
  or or_1 (or_5_out[2], done_stay, en_S_res, sel_E_work, sel_M_work[1]);
  and and_2 (and_2_out, sel_M_work[1], ~round_unnorm);  // AND_Gate
  and and_3 (and_3_out, sel_M_work[1], round_unnorm);
  Register #(.width(3)) state (.D(or_5_out), .en(1'b1), .clk(Clk), .Q(state_q), .clr(Rst));
  or or_2 (en_E_work, en_align, sel_E_work);
  or or_3 (en_M_work, en_S_res, sel_E_work, and_3_out);
  Decoder #(.select(3)) decoder_1 (
    .out0(is_IDLE), .out1(load_regs), .out2(en_align), .out3(en_S_res), .out4(sel_E_work),
    .out5(sel_M_work[1]), .out6(Done), .sel(state_q), .en(1'b1));  // open: out7
  and and_4 (and_4_out, sel_E_work, exception);
  or or_4 (or_5_out[1], and_2_out, and_4_out, load_regs, en_align, done_stay);
  and and_5 (and_5_out, is_IDLE, Start);
  or or_5 (or_5_out[0], and_5_out, en_align, and_6_out, and_7_out);
  and and_6 (and_6_out, sel_E_work, nor_1_out, ~exception);  // AND_Gate
  nor nor_1 (nor_1_out, need_right, need_left);
  and and_7 (and_7_out, Start, Done);

  assign sel_M_work[0] = sel_E_work;

  // Other names for the same wires on the sheet: is_ADD = en_S_res; is_ALIGN = en_align; is_DONE = Done;
  //   is_UNPACK = load_regs; is_NORMALIZE = sel_E_work; is_ROUND = sel_M_work[1]
endmodule
